# Fritzing sketch Untitled Sketch 2 (saved by Fritzing 1.0.6)
breadboards: 1

parts:
  MH-ET_LIVE_ESP32_DEVKIT1 = MH-ET LIVE ESP32 DEVKIT 38 pins
  DHT1 = DHT22 Humidity and Temperature Sensor
  DS1 = DS18B20 1-Wire Temperature Sensor [part_number=DS18B20]
  R1 = Resistor [tolerance=±5% resistance=220 package="1206 [SMD]"]
  Mod2 = Voltage Sensor 25V
  D1 = SOLAR-IXYS [package=solarbit-12x1]
  Part1 = Current Sensor 5A
  LED1 = Red LED - Rect 5x2x7mm [package="5x2x7 mm [THT]"]
  R2 = Resistor [tolerance=±5% resistance=220 package="1206 [SMD]"]
  R3 = Resistor [tolerance=±5% resistance=10k package="1206 [SMD]"]
  R4 = Resistor [tolerance=±5% resistance=10k package="1206 [SMD]"]
  R5 = Resistor [tolerance=±5% resistance=10k package="1206 [SMD]"]
  M1 = 1 chan 5v relay module
  Q1 = NPN-Transistor [package="TO92 [THT]"]  # not connected
  R6 = Resistor [tolerance=±5% resistance=220 package="1206 [SMD]"]
  R7 = Resistor [tolerance=±5% resistance=220 package="1206 [SMD]"]
  R8 = Photocell (LDR) [power=0.25W dark_resistance_@0.01lx=300kΩ light_resistance_@100lx=400Ω luminance=10lx package=THT]
  R9 = Resistor [tolerance=±5% resistance=220 package="1206 [SMD]"]
  R10 = Resistor [tolerance=±5% resistance=10k package="1206 [SMD]"]  # not connected
  R11 = Resistor [tolerance=±5% resistance=220 package="1206 [SMD]"]

nets:
  N1: MH-ET_LIVE_ESP32_DEVKIT1.IO34, Mod2.S
  N2: MH-ET_LIVE_ESP32_DEVKIT1.IO35, R1.Pin_1
  N3: MH-ET_LIVE_ESP32_DEVKIT1.IO32, DHT1.DATA
  N4: MH-ET_LIVE_ESP32_DEVKIT1.IO33, R8.pin_1
  GND: MH-ET_LIVE_ESP32_DEVKIT1.GND, DHT1.GND, R1.Pin_0, Mod2.GND, Mod2.-, D1.A, Part1.GND, LED1.cathode, R4.Pin_1, M1.pin_2, R9.Pin_1, R11.Pin_1
  VDD: MH-ET_LIVE_ESP32_DEVKIT1.5V, DHT1.VDD, DS1.VDD, Mod2.+, Part1.VCC, M1.pin_1, R6.Pin_0, R8.pin_0
  N5: MH-ET_LIVE_ESP32_DEVKIT1.RXD0, R5.Pin_0
  N6: MH-ET_LIVE_ESP32_DEVKIT1.IO21, R7.Pin_1
  N7: Mod2.VCC, D1.C
  N8: Part1.1, M1.pin_5
  N9: Part1.2, Part1.OUT, R2.Pin_1, R3.Pin_0
  N10: LED1.anode, M1.pin_6
  N11: M1.pin_3, R6.Pin_1

notes:
  DHT22--->Pin 4
  LDR--->36
  THERMISTOR- ->>13
  voltage_s-->39
  Current_s-->34
  Relay-->14

custom parts:
  MH-ET LIVE ESP32 DEVKIT 38 pins: http://mh.nodebb.com/topic/2/mh-et-live-esp32-devkit
  Red LED - Rect 5x2x7mm: A generic rectangular red LED (~1.8V) 5mm x 2mm x 7mm
  1 chan 5v relay module: 1 Channel 5V Relay Module Board Shield with Optocoupler Support High and Low Level Trigger for Arduino.
